# Fritzing sketch UV SENSOR (saved by Fritzing 0.9.3b)
breadboards: 1

parts:
  BATTERY = LIPO-1000mAh [package=lipo-1000]
  SWITCH = Toggle Switch [package=THT]
  STEP_UP = RioRand LM2596
  UV_SENSOR = Header 3 [package=1x03-1mm-ra]
  ARDUINO_NANO = Arduino Nano (Rev3.0)

nets:
  N1: BATTERY.+, STEP_UP.Pin_1
  N2: BATTERY.-, STEP_UP.Pin_2
  N3: SWITCH.L1, STEP_UP.Pin_3
  N4: SWITCH.COM, UV_SENSOR.2, ARDUINO_NANO.5V
  N5: STEP_UP.Pin_4, UV_SENSOR.1, ARDUINO_NANO.GND
  N6: UV_SENSOR.3, ARDUINO_NANO.A0

notes:
  UV Sensor - UVM-30A
  _PINS: _
  * OUT A0
  * + 5V
  * - GND
